# Fritzing sketch AutoTea (saved by Fritzing 0.9.3b)
breadboards: 1

parts:
  Part1 = Arduino Mega 2560 (Rev3)
  R1 = Resistor [tolerance=±5% resistance=10k package="0805 [SMD]"]  # not connected
  U2 = LCD-16X2 [package=lcd-16x2]
  S1 = Pushbutton [package="[SMD]"]
  LED1 = RGB LED - (4 legs) [package="5 mm [THT]"]
  U1 = POT [package=pot_alpha_rv16af-20]

nets:
  5V: Part1.D12_PWM, Part1.5V, U2.VDD, U2.VO, U2.DB7, U2.A, U1.S, U1.E
  N1: Part1.D11_PWM, U2.DB6
  N2: Part1.D10_PWM, U2.DB5
  N3: Part1.D9_PWM, U2.DB3, U2.DB4
  N4: Part1.D8_PWM, U2.E, U2.DB0
  GND: Part1.GND, U2.VSS, U2.K, S1.Pin_2, U1.A
  N5: Part1.D7_PWM, U2.RS, U2.R_W
  N6: Part1.D48, LED1.blue_cathode
  N7: Part1.D50, LED1.green_cathode
  N8: Part1.D52, LED1.red_cathode
  N9: Part1.D53, S1.Pin_3, S1.Pin_4
